# Fritzing sketch modulo_controle (saved by Fritzing 0.9.3b)
breadboards: 1

parts:
  ARDUINO = Arduino Uno (Rev3)
  MODULO_SD = MicroSD Card Module
  CASA_1 = RJ45 Jack [package=rj45-8]
  CASA_2 = RJ45 Jack [package=rj45-8]
  CASA_3 = RJ45 Jack [package=rj45-8]
  RTC = Real Time Clock Module - DS1307 RTC Breakout Board
  LED_VERMELHO = LTE-302 [package=lte-302]
  R1 = Resistor [tolerance=±5% resistance=220 package="2512 [SMD]"]
  LED_VERDE = LTE-302 [package=lte-302]
  R2 = Resistor [tolerance=±5% resistance=220 package="2512 [SMD]"]

nets:
  N1: ARDUINO.A1, CASA_1.6
  N2: ARDUINO.A2, CASA_2.6
  N3: ARDUINO.A3, CASA_3.6
  N4: ARDUINO.A4/SDA, RTC.SDA
  N5: ARDUINO.A5/SCL, RTC.SCL
  R1: ARDUINO.D8
  R2: ARDUINO.D9_PWM
  N6: ARDUINO.D10_PWM/SS, MODULO_SD.CS
  N7: ARDUINO.D11_PWM/MOSI, MODULO_SD.MOSI
  N8: ARDUINO.D12/MISO, MODULO_SD.MISO
  N9: ARDUINO.D13/SCK, MODULO_SD.SCK
  GND: ARDUINO.GND, MODULO_SD.GND, CASA_1.4, CASA_1.8, CASA_2.4, CASA_2.8, CASA_3.4, CASA_3.8, RTC.GND, LED_VERMELHO.C, LED_VERDE.C
  N10: ARDUINO.D2, CASA_1.2
  N11: ARDUINO.D3_PWM, CASA_1.3
  N12: ARDUINO.D4, CASA_2.2
  N13: ARDUINO.D5_PWM, CASA_2.3
  N14: ARDUINO.D6_PWM, CASA_3.2
  N15: ARDUINO.D7, CASA_3.3
  5V: ARDUINO.5V, MODULO_SD.VCC, CASA_1.1, CASA_1.5, CASA_2.1, CASA_2.5, CASA_3.1, CASA_3.5, RTC.5V
  N16: LED_VERMELHO.A, R1.Pin_0
  Arduino_D8: R1.Pin_1
  N17: LED_VERDE.A, R2.Pin_0
  Arduino_D9: R2.Pin_1
