# Fritzing sketch modulo_sensores (saved by Fritzing 0.9.3b)

parts:
  HDC_1080 = Humidity Temperature Sensor SHT15
  MLX90614 = MLX90614 [package=to-39]
  KY-038 = Breakout Board for Electret Microphone
  CENTRAL = RJ45 Jack [package=rj45-8]

nets:
  GND: HDC_1080.GND, MLX90614.VSS, KY-038.GND, CENTRAL.4, CENTRAL.8
  N1: HDC_1080.SCL, MLX90614.SCL_VZ, CENTRAL.3
  N2: HDC_1080.SDA, MLX90614.PWM_SDA, CENTRAL.2
  5V: HDC_1080.VCC, MLX90614.VDD, KY-038.VCC, CENTRAL.1, CENTRAL.5
  N3: KY-038.AUD, CENTRAL.6

custom parts:
  Humidity Temperature Sensor SHT15: Description: This is a simple breakout board for the SHT15 humidity sensor from Sensirion. The SHT15 digital humidity and temperature sensor is fully calibrated and offers high precision and excellent long-term stability at low cost. The digital CMOSens Technology integrates two sensors and readout circuitry on one single chip. These sensors are really impressive! Very sensitive and straight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
